// Logisim project branch-comp.circ as structural Verilog: 1 circuit, main circuit branch_comp
module branch_comp (
  input  [31:0] BrData1,
  input  [31:0] BrData2,
  input  BrUn,
  output BrEq,
  output BrLt
);

  wire and_1_out, and_2_out, and_3_out, and_4_out, BrEq_2C, BrEq_unsigned, BrLt_2C, BrLt_unsigned, not_1_out,
       not_2_out;

  not not_1 (not_1_out, BrUn);
  not not_2 (not_2_out, BrUn);
  Comparator #(.width(32)) comparator_1 (.a(BrData1), .b(BrData2), .eq(BrEq_2C), .lt(BrLt_2C));  // open: gt
  Comparator #(.mode("unsigned"), .width(32)) comparator_2 (
    .a(BrData1), .b(BrData2), .eq(BrEq_unsigned), .lt(BrLt_unsigned));  // open: gt
  and and_1 (and_1_out, BrEq_2C, not_1_out);
  and and_2 (and_2_out, BrEq_unsigned, BrUn);
  and and_3 (and_3_out, BrLt_unsigned, BrUn);
  and and_4 (and_4_out, BrLt_2C, not_2_out);
  or or_1 (BrEq, and_1_out, and_2_out);
  or or_2 (BrLt, and_3_out, and_4_out);

  // Notes on the sheet:
  //   INPUTS to your circuit
  //   DON'T CHANGE THE LOCATIONS OF THE INPUTS AND OUTPUTS!
  //   OUTPUT from your circuit
endmodule
