// Logisim project control-logic.circ as structural Verilog: 1 circuit, main circuit control_logic
module control_logic (
  input  [31:0] Instruction,
  input  BrEq,
  input  BrLt,
  output PCSel,
  output RegWEn,
  output [2:0] ImmSel,
  output BrUn,
  output ASel,
  output BSel,
  output [3:0] ALUSel,
  output MemWEn,
  output [1:0] WBSel
);

  wire and_42_out, and_43_out, and_44_out, and_45_out, and_46_out, and_47_out, comparator_6_eq,
       comparator_7_eq, comparator_8_eq, comparator_9_eq, comparator_10_eq, comparator_11_eq,
       comparator_12_eq, comparator_13_eq, comparator_14_eq, comparator_15_eq, comparator_16_eq,
       comparator_17_eq, comparator_18_eq, comparator_19_eq, comparator_20_eq, comparator_21_eq,
       comparator_22_eq, comparator_23_eq, comparator_24_eq, comparator_25_eq, comparator_26_eq,
       comparator_27_eq, comparator_28_eq, comparator_29_eq, comparator_30_eq, comparator_31_eq,
       comparator_32_eq, comparator_33_eq, comparator_34_eq, comparator_35_eq, comparator_36_eq,
       comparator_37_eq, has0outputI, has20outputI, is_0_f3_R, is_0_f7_R, is_1_f3_R, is_1_f7_R, is_5_f3_R,
       is_20_f7_R, is_add, is_addi, is_and, is_andi, is_auipc, is_B_type, is_beq, is_bge, is_bgeu, is_blt,
       is_bltu, is_bne, is_I_type, is_jal, is_jalr, is_lb, is_lh, is_Load, is_lui, is_lw, is_mul, is_mulh,
       is_mulhu, is_or, is_ori, is_R_type, is_S_type, is_sb, is_sh, is_sll, is_slli, is_slt, is_slti, is_sra,
       is_srai, is_srali, is_srl, is_srli, is_sub, is_sw, is_xor, is_xori, not_1_out, not_2_out, not_3_out,
       pr1used, pr2used, rom_sel;
  wire [1:0] priority_encoder_3_out;
  wire [2:0] Funct3I, Funct3L, Funct3R, Funct3S, type_sel;
  wire [4:0] priority_encoder_2_out;
  wire [5:0] bit_extender_1_out, pri1op, pri2op, rom_input;
  wire [6:0] Funct7I, Funct7R;
  wire [15:14] rom_1_data;
  wire [24:0] I_Instruct, R_Instruct;
  wire [31:0] B_Instruct, Load_Instruct, S_Instruct;

  Comparator #(.width(7)) comparator_1 (.a(Instruction[6:0]), .b(7'b0010111), .eq(is_auipc));  // open: gt, lt
  Comparator #(.width(7)) comparator_2 (.a(Instruction[6:0]), .b(7'b1101111), .eq(is_jal));  // open: gt, lt
  Comparator #(.width(7)) comparator_3 (.a(Instruction[6:0]), .b(7'b1100111), .eq(is_jalr));  // open: gt, lt
  Comparator #(.width(7)) comparator_4 (.a(Instruction[6:0]), .b(7'b0100011), .eq(is_S_type));  // open: gt, lt
  Comparator #(.width(7)) comparator_5 (.a(Instruction[6:0]), .b(7'b0110111), .eq(is_lui));  // open: gt, lt
  Comparator #(.mode("unsigned"), .width(3)) comparator_6 (
    .a(Funct3I), .b(3'b000), .eq(comparator_6_eq));  // open: gt, lt
  Comparator #(.mode("unsigned"), .width(3)) comparator_7 (
    .a(Funct3I), .b(3'b001), .eq(comparator_7_eq));  // open: gt, lt
  Comparator #(.mode("unsigned"), .width(3)) comparator_8 (
    .a(Funct3I), .b(3'b010), .eq(comparator_8_eq));  // open: gt, lt
  Comparator #(.mode("unsigned"), .width(3)) comparator_9 (
    .a(Funct3I), .b(3'b100), .eq(comparator_9_eq));  // open: gt, lt
  Comparator #(.mode("unsigned"), .width(3)) comparator_10 (
    .a(Funct3I), .b(3'b101), .eq(comparator_10_eq));  // open: gt, lt
  Comparator #(.mode("unsigned"), .width(3)) comparator_11 (
    .a(Funct3I), .b(3'b110), .eq(comparator_11_eq));  // open: gt, lt
  Comparator #(.mode("unsigned"), .width(3)) comparator_12 (
    .a(Funct3I), .b(3'b111), .eq(comparator_12_eq));  // open: gt, lt
  Comparator #(.mode("unsigned"), .width(7)) comparator_13 (
    .a(Funct7I), .b(7'b0100000), .eq(comparator_13_eq));  // open: gt, lt
  Comparator #(.mode("unsigned"), .width(7)) comparator_14 (
    .a(Funct7I), .b({7{1'b0}}), .eq(comparator_14_eq));  // open: gt, lt
  Comparator #(.mode("unsigned"), .width(3)) comparator_15 (
    .a(B_Instruct[14:12]), .b(3'b000), .eq(comparator_15_eq));  // open: gt, lt
  Comparator #(.mode("unsigned"), .width(3)) comparator_16 (
    .a(B_Instruct[14:12]), .b(3'b001), .eq(comparator_16_eq));  // open: gt, lt
  Comparator #(.mode("unsigned"), .width(3)) comparator_17 (
    .a(B_Instruct[14:12]), .b(3'b100), .eq(comparator_17_eq));  // open: gt, lt
  Comparator #(.mode("unsigned"), .width(3)) comparator_18 (
    .a(B_Instruct[14:12]), .b(3'b101), .eq(comparator_18_eq));  // open: gt, lt
  Comparator #(.mode("unsigned"), .width(3)) comparator_19 (
    .a(B_Instruct[14:12]), .b(3'b110), .eq(comparator_19_eq));  // open: gt, lt
  Comparator #(.mode("unsigned"), .width(3)) comparator_20 (
    .a(B_Instruct[14:12]), .b(3'b111), .eq(comparator_20_eq));  // open: gt, lt
  Comparator #(.mode("unsigned"), .width(3)) comparator_21 (
    .a(Funct3L), .b(3'b000), .eq(comparator_21_eq));  // open: gt, lt
  Comparator #(.mode("unsigned"), .width(3)) comparator_22 (
    .a(Funct3L), .b(3'b001), .eq(comparator_22_eq));  // open: gt, lt
  Comparator #(.mode("unsigned"), .width(3)) comparator_23 (
    .a(Funct3L), .b(3'b010), .eq(comparator_23_eq));  // open: gt, lt
  Comparator #(.mode("unsigned"), .width(3)) comparator_24 (
    .a(Funct3S), .b(3'b000), .eq(comparator_24_eq));  // open: gt, lt
  Comparator #(.mode("unsigned"), .width(3)) comparator_25 (
    .a(Funct3S), .b(3'b001), .eq(comparator_25_eq));  // open: gt, lt
  Comparator #(.mode("unsigned"), .width(3)) comparator_26 (
    .a(Funct3S), .b(3'b010), .eq(comparator_26_eq));  // open: gt, lt
  ROM #(.addrWidth(6), .dataWidth(16)) rom_1 (
    .addr(rom_input), .data({rom_1_data, WBSel, MemWEn, ALUSel, BSel, ASel, BrUn, ImmSel, RegWEn}));
  and and_1 (is_slli, is_I_type, comparator_7_eq);
  and and_2 (is_slti, is_I_type, comparator_8_eq);
  and and_3 (is_xori, is_I_type, comparator_9_eq);
  and and_4 (is_srali, is_I_type, comparator_10_eq);
  and and_5 (is_ori, is_I_type, comparator_11_eq);
  and and_6 (is_andi, is_I_type, comparator_12_eq);
  and and_7 (has20outputI, is_I_type, comparator_13_eq);
  and and_8 (has0outputI, is_I_type, comparator_14_eq);
  Comparator #(.mode("unsigned"), .width(3)) comparator_27 (
    .a(Funct3R), .b(3'b000), .eq(comparator_27_eq));  // open: gt, lt
  Comparator #(.mode("unsigned"), .width(3)) comparator_28 (
    .a(Funct3R), .b(3'b001), .eq(comparator_28_eq));  // open: gt, lt
  Comparator #(.mode("unsigned"), .width(3)) comparator_29 (
    .a(Funct3R), .b(3'b010), .eq(comparator_29_eq));  // open: gt, lt
  Comparator #(.mode("unsigned"), .width(3)) comparator_30 (
    .a(Funct3R), .b(3'b011), .eq(comparator_30_eq));  // open: gt, lt
  Comparator #(.mode("unsigned"), .width(3)) comparator_31 (
    .a(Funct3R), .b(3'b100), .eq(comparator_31_eq));  // open: gt, lt
  Comparator #(.mode("unsigned"), .width(3)) comparator_32 (
    .a(Funct3R), .b(3'b101), .eq(comparator_32_eq));  // open: gt, lt
  Comparator #(.mode("unsigned"), .width(3)) comparator_33 (
    .a(Funct3R), .b(3'b110), .eq(comparator_33_eq));  // open: gt, lt
  Comparator #(.mode("unsigned"), .width(3)) comparator_34 (
    .a(Funct3R), .b(3'b111), .eq(comparator_34_eq));  // open: gt, lt
  Comparator #(.width(7)) comparator_35 (.a(Funct7R), .b({7{1'b0}}), .eq(comparator_35_eq));  // open: gt, lt
  Comparator #(.width(7)) comparator_36 (.a(Funct7R), .b(7'b0000001), .eq(comparator_36_eq));  // open: gt, lt
  Comparator #(.width(7)) comparator_37 (.a(Funct7R), .b(7'b0100000), .eq(comparator_37_eq));  // open: gt, lt
  and and_9 (is_sw, is_S_type, comparator_26_eq);
  Comparator #(.width(7)) comparator_38 (.a(Instruction[6:0]), .b(7'b0010011), .eq(is_I_type));  // open: gt, lt
  Comparator #(.width(7)) comparator_39 (.a(Instruction[6:0]), .b(7'b0110011), .eq(is_R_type));  // open: gt, lt
  Comparator #(.width(7)) comparator_40 (.a(Instruction[6:0]), .b(7'b1100011), .eq(is_B_type));  // open: gt, lt
  Comparator #(.width(7)) comparator_41 (.a(Instruction[6:0]), .b(7'b0000011), .eq(is_Load));  // open: gt, lt
  and and_10 (is_addi, is_I_type, comparator_6_eq);
  and and_11 (is_0_f3_R, is_R_type, comparator_27_eq);
  and and_12 (is_1_f3_R, is_R_type, comparator_28_eq);
  and and_13 (is_slt, is_R_type, comparator_29_eq);
  and and_14 (is_mulhu, is_R_type, comparator_30_eq);
  and and_15 (is_xor, is_R_type, comparator_31_eq);
  and and_16 (is_5_f3_R, is_R_type, comparator_32_eq);
  and and_17 (is_or, is_R_type, comparator_33_eq);
  and and_18 (is_and, is_R_type, comparator_34_eq);
  and and_19 (is_0_f7_R, is_R_type, comparator_35_eq);
  and and_20 (is_1_f7_R, is_R_type, comparator_36_eq);
  and and_21 (is_20_f7_R, is_R_type, comparator_37_eq);
  and and_22 (is_beq, is_B_type, comparator_15_eq);
  and and_23 (is_bne, is_B_type, comparator_16_eq);
  and and_24 (is_blt, is_B_type, comparator_17_eq);
  and and_25 (is_bge, is_B_type, comparator_18_eq);
  and and_26 (is_bltu, is_B_type, comparator_19_eq);
  and and_27 (is_bgeu, is_B_type, comparator_20_eq);
  and and_28 (is_lb, is_Load, comparator_21_eq);
  and and_29 (is_lh, is_Load, comparator_22_eq);
  and and_30 (is_lw, is_Load, comparator_23_eq);
  and and_31 (is_sb, is_S_type, comparator_24_eq);
  and and_32 (is_sh, is_S_type, comparator_25_eq);
  and and_33 (is_srai, is_srali, has20outputI);
  and and_34 (is_srli, is_srali, has0outputI);
  and and_35 (is_add, is_0_f3_R, is_0_f7_R);
  and and_36 (is_mul, is_0_f3_R, is_1_f7_R);
  and and_37 (is_sub, is_0_f3_R, is_20_f7_R);
  and and_38 (is_sll, is_1_f3_R, is_0_f7_R);
  and and_39 (is_mulh, is_1_f3_R, is_1_f7_R);
  and and_40 (is_srl, is_5_f3_R, is_0_f7_R);
  and and_41 (is_sra, is_5_f3_R, is_20_f7_R);
  Priority_Encoder priority_encoder_1 (
    .in0(is_I_type), .in1(is_R_type), .in2(is_B_type), .in3(is_Load), .in4(is_S_type), .out(type_sel));  // open: in5, in6, in7, en_in, gs, en_out
  Demultiplexer #(.enable("false"), .select(3), .width(32)) demultiplexer_1 (
    .out0({Funct7I, I_Instruct[24:15], Funct3I, I_Instruct[11:0]}),
    .out1({Funct7R, R_Instruct[24:15], Funct3R, R_Instruct[11:0]}), .out2(B_Instruct),
    .out3({Load_Instruct[31:15], Funct3L, Load_Instruct[11:0]}),
    .out4({S_Instruct[31:15], Funct3S, S_Instruct[11:0]}), .in(Instruction), .sel(type_sel));  // open: out5, out6, out7
  Priority_Encoder #(.select(5)) priority_encoder_2 (
    .in0(is_add), .in1(is_mul), .in2(is_sub), .in3(is_sll), .in4(is_mulh), .in5(is_mulhu), .in6(is_slt),
    .in7(is_xor), .in8(is_srl), .in9(is_sra), .in10(is_or), .in11(is_and), .in12(is_lb), .in13(is_lh),
    .in14(is_lw), .in15(is_addi), .in16(is_slli), .in17(is_slti), .in18(is_xori), .in19(is_srli),
    .in20(is_srai), .in21(is_ori), .in22(is_andi), .in23(is_sb), .in24(is_sh), .in25(is_sw), .in26(is_beq),
    .in27(is_bne), .in28(is_blt), .in29(is_bge), .in30(is_bltu), .in31(is_bgeu),
    .out(priority_encoder_2_out), .gs(pr1used));  // open: en_out, en_in
  Priority_Encoder #(.select(2)) priority_encoder_3 (
    .in0(is_auipc), .in1(is_lui), .in2(is_jal), .in3(is_jalr), .out(priority_encoder_3_out), .gs(pr2used));  // open: en_out, en_in
  assign bit_extender_1_out = {{4{1'b0}}, priority_encoder_3_out};  // Bit_Extender bit_extender_1
  Priority_Encoder #(.select(1)) priority_encoder_4 (
    .in0(pr1used), .in1(pr2used), .out(rom_sel));  // open: gs, en_out, en_in
  not not_1 (not_1_out, BrEq);
  not not_2 (not_2_out, BrLt);
  not not_3 (not_3_out, BrLt);
  assign pri1op = {{1{1'b0}}, priority_encoder_2_out};  // Bit_Extender bit_extender_2
  Adder #(.width(6)) adder_1 (.a(bit_extender_1_out), .b(6'b100000), .out(pri2op));  // open: cin, cout
  and and_42 (and_42_out, is_bne, not_1_out);
  and and_43 (and_43_out, is_beq, BrEq);
  and and_44 (and_44_out, is_blt, BrLt);
  and and_45 (and_45_out, is_bge, not_2_out);
  and and_46 (and_46_out, is_bgeu, not_3_out);
  and and_47 (and_47_out, is_bltu, BrLt);
  Multiplexer #(.enable("false"), .width(6)) multiplexer_1 (.in0(pri1op), .in1(pri2op), .out(rom_input), .sel(rom_sel));
  or or_1 (PCSel, is_jalr, and_42_out, and_43_out, and_44_out, and_45_out, and_46_out, and_47_out, is_jal);

  // Other names for the same wires on the sheet: Funct3B[2:0] = B_Instruct[14:12];
  //   I_Instruct (some bits) = {Funct7I, Funct3I}; opcode[6:0] = Instruction[6:0]; Load_Instruct[14:12] = Funct3L;
  //   R_Instruct (some bits) = {Funct7R, Funct3R}; S_Instruct[14:12] = Funct3S

  // Notes on the sheet:
  //   INPUTS to your circuit
  //   Connect ROM Input here ->
  //   contents of rom_1 (hex, n*v repeats v):
  //   1001 1401 1601 1081 1481 1581 1101 1201 1281 1681 1301 1381 41 41 41 1041 10c1 1141 1241 12c1 16c1
  //   1341 13c1 1842 1842 1842 4*1064 1074 1074 1067 17e7 2069 2041
  //   ROM FOR CONTROL LOGIC
  //   DON'T CHANGE THE LOCATIONS OF THE INPUTS AND OUTPUTS!
  //   This is only if you choose to do the ROM option
  //   CONNECT
  //   WIRE
  //   TO
  //   USE
  //   ROM
  //   OUTPUT from your circuit
  //   Reminder: If using ROM, use combinational logic for PCSel
endmodule
