// Logisim project imm-gen.circ as structural Verilog: 1 circuit, main circuit imm_gen
module imm_gen (
  input  [31:0] Instruction,
  input  [2:0] ImmSel,
  output [31:0] Immediate
);

  wire imm_20J, imm_31J;
  wire [7:0] imm_12to19J;
  wire [9:0] imm_21to30J;
  wire [11:0] J_type, U_type;
  wire [31:0] B_type, I_type, Immediate_I, Immediate_S, S_type;
  wire [31:12] Immediate_B, Immediate_U;
  wire [31:20] Immediate_J;

  Demultiplexer #(.enable("false"), .select(3), .width(32)) demultiplexer_1 (
    .out0(I_type), .out1(S_type), .out2(B_type), .out3({Immediate_U, U_type}),
    .out4({imm_31J, imm_21to30J, imm_20J, imm_12to19J, J_type}), .in(Instruction), .sel(ImmSel));  // open: out5, out6, out7
  assign Immediate_I = {{20{I_type[31]}}, I_type[31:20]};  // Bit_Extender bit_extender_1
  assign Immediate_J = {{11{imm_31J}}, imm_31J};  // Bit_Extender bit_extender_2
  assign Immediate_S = {{20{S_type[31]}}, {S_type[31:25], S_type[11:7]}};  // Bit_Extender bit_extender_3
  Multiplexer #(.enable("false"), .select(3), .width(32)) multiplexer_1 (
    .in0(Immediate_I), .in1(Immediate_S), .in2({Immediate_B, B_type[7], B_type[30:25], B_type[11:8], 1'b0}),
    .in3({Immediate_U, {12{1'b0}}}), .in4({Immediate_J, imm_12to19J, imm_20J, imm_21to30J, 1'b0}),
    .out(Immediate), .sel(ImmSel));  // open: in5, in6, in7
  assign Immediate_B = {{19{B_type[31]}}, B_type[31]};  // Bit_Extender bit_extender_4

  // Other names for the same wires on the sheet: imm_twelveB = B_type[31]; imm_oneToFourB[3:0] = B_type[11:8];
  //   Immediate_B[11:1] = {B_type[7], B_type[30:25], B_type[11:8]}; imm_fiveToTenB[5:0] = B_type[30:25];
  //   imm_elevenB = B_type[7]; Immediate_J[19:1] = {imm_12to19J, imm_20J, imm_21to30J};
  //   J_type[31:12] = {imm_31J, imm_21to30J, imm_20J, imm_12to19J}; U_type[31:12] = Immediate_U

  // Notes on the sheet:
  //   INPUTS to your circuit
  //   DON'T CHANGE THE LOCATIONS OF THE INPUTS AND OUTPUTS!
  //   OUTPUT from your circuit
endmodule
