// Logisim project partial-load.circ as structural Verilog: 1 circuit, main circuit partial_load
module partial_load (
  input  [31:0] Instruction,
  input  [31:0] MemAddress,
  input  [31:0] DataFromMem,
  output [31:0] DataToReg
);

  wire comparator_4_eq, comparator_5_eq, comparator_6_eq, comparator_7_eq, comparator_8_eq, comparator_9_eq,
       comparator_10_eq, comparator_11_eq, is_lb, is_lb00, is_lb01, is_lb10, is_lb11, is_lh, is_lh00,
       is_lh01, is_lh10, is_lw, is_lw00;
  wire [2:0] sel;
  wire [31:0] bit_extender_1_out, bit_extender_2_out, bit_extender_3_out, bit_extender_4_out,
       bit_extender_5_out, bit_extender_6_out, bit_extender_7_out;

  Comparator #(.width(3)) comparator_1 (.a(Instruction[14:12]), .b(3'b000), .eq(is_lb));  // open: gt, lt
  Comparator #(.width(3)) comparator_2 (.a(Instruction[14:12]), .b(3'b001), .eq(is_lh));  // open: gt, lt
  Comparator #(.width(3)) comparator_3 (.a(Instruction[14:12]), .b(3'b010), .eq(is_lw));  // open: gt, lt
  Comparator #(.width(2)) comparator_4 (.a(MemAddress[1:0]), .b(2'b00), .eq(comparator_4_eq));  // open: gt, lt
  Comparator #(.width(2)) comparator_5 (.a(MemAddress[1:0]), .b(2'b01), .eq(comparator_5_eq));  // open: gt, lt
  Comparator #(.width(2)) comparator_6 (.a(MemAddress[1:0]), .b(2'b10), .eq(comparator_6_eq));  // open: gt, lt
  Comparator #(.width(2)) comparator_7 (.a(MemAddress[1:0]), .b(2'b11), .eq(comparator_7_eq));  // open: gt, lt
  Comparator #(.width(2)) comparator_8 (.a(MemAddress[1:0]), .b(2'b00), .eq(comparator_8_eq));  // open: gt, lt
  Comparator #(.width(2)) comparator_9 (.a(MemAddress[1:0]), .b(2'b01), .eq(comparator_9_eq));  // open: gt, lt
  Comparator #(.width(2)) comparator_10 (.a(MemAddress[1:0]), .b(2'b10), .eq(comparator_10_eq));  // open: gt, lt
  Comparator #(.width(2)) comparator_11 (.a(MemAddress[1:0]), .b(2'b00), .eq(comparator_11_eq));  // open: gt, lt
  and and_1 (is_lb00, comparator_4_eq, is_lb);
  and and_2 (is_lb01, comparator_5_eq, is_lb);
  and and_3 (is_lb10, comparator_6_eq, is_lb);
  and and_4 (is_lb11, comparator_7_eq, is_lb);
  and and_5 (is_lh00, comparator_8_eq, is_lh);
  and and_6 (is_lh01, comparator_9_eq, is_lh);
  and and_7 (is_lh10, comparator_10_eq, is_lh);
  and and_8 (is_lw00, comparator_11_eq, is_lw);
  assign bit_extender_1_out = {{24{DataFromMem[31]}}, DataFromMem[31:24]};  // Bit_Extender bit_extender_1
  assign bit_extender_2_out = {{16{DataFromMem[15]}}, DataFromMem[15:0]};  // Bit_Extender bit_extender_2
  assign bit_extender_3_out = {{16{DataFromMem[23]}}, DataFromMem[23:8]};  // Bit_Extender bit_extender_3
  assign bit_extender_4_out = {{16{DataFromMem[31]}}, DataFromMem[31:16]};  // Bit_Extender bit_extender_4
  assign bit_extender_5_out = {{24{DataFromMem[23]}}, DataFromMem[23:16]};  // Bit_Extender bit_extender_5
  Priority_Encoder priority_encoder_1 (
    .in0(is_lb00), .in1(is_lb01), .in2(is_lb10), .in3(is_lb11), .in4(is_lh00), .in5(is_lh01), .in6(is_lh10),
    .in7(is_lw00), .out(sel));  // open: en_in, gs, en_out
  assign bit_extender_6_out = {{24{DataFromMem[7]}}, DataFromMem[7:0]};  // Bit_Extender bit_extender_6
  assign bit_extender_7_out = {{24{DataFromMem[15]}}, DataFromMem[15:8]};  // Bit_Extender bit_extender_7
  Multiplexer #(.enable("false"), .select(3), .width(32)) multiplexer_1 (
    .in0(bit_extender_6_out), .in1(bit_extender_7_out), .in2(bit_extender_5_out), .in3(bit_extender_1_out),
    .in4(bit_extender_2_out), .in5(bit_extender_3_out), .in6(bit_extender_4_out), .in7(DataFromMem),
    .out(DataToReg), .sel(sel));

  // Other names for the same wires on the sheet: lb00_data[7:0] = DataFromMem[7:0];
  //   lh00_data[15:0] = DataFromMem[15:0]; lb01_data[7:0] = DataFromMem[15:8]; lh01_data[15:0] = DataFromMem[23:8];
  //   lb10_data[7:0] = DataFromMem[23:16]; lh10_data[15:0] = DataFromMem[31:16]; lb11_data[7:0] = DataFromMem[31:24];
  //   func3[2:0] = Instruction[14:12]; bot2ofMA[1:0] = MemAddress[1:0]

  // Notes on the sheet:
  //   INPUTS to your circuit
  //   DON'T CHANGE THE LOCATIONS OF THE INPUTS AND OUTPUTS!
  //   OUTPUT from your circuit
endmodule
