// Logisim project regfile.circ as structural Verilog: 1 circuit, main circuit regfile
module regfile (
  input  [4:0] ReadReg1,
  input  [4:0] ReadReg2,
  input  [4:0] WriteReg,
  input  [31:0] RegWriteData,
  input  RegWEn,
  input  clk,
  output [31:0] ra,
  output [31:0] sp,
  output [31:0] t0,
  output [31:0] t1,
  output [31:0] t2,
  output [31:0] s0,
  output [31:0] s1,
  output [31:0] a0,
  output [31:0] RegReadData1,
  output [31:0] RegReadData2
);

  wire we1, we2, we3, we4, we5, we6, we7, we8, we9, we10, we11, we12, we13, we14, we15, we16, we17, we18,
       we19, we20, we21, we22, we23, we24, we25, we26, we27, we28, we29, we30, we31;
  wire [31:0] a1, a2, a3, a4, a5, a6, a7, gp, s2, s3, s4, s5, s6, s7, s8, s9, s10, s11, t3, t4, t5, t6, tp,
       x0;

  Decoder #(.select(5)) decoder_1 (
    .out1(we1), .out2(we2), .out3(we3), .out4(we4), .out5(we5), .out6(we6), .out7(we7), .out8(we8),
    .out9(we9), .out10(we10), .out11(we11), .out12(we12), .out13(we13), .out14(we14), .out15(we15),
    .out16(we16), .out17(we17), .out18(we18), .out19(we19), .out20(we20), .out21(we21), .out22(we22),
    .out23(we23), .out24(we24), .out25(we25), .out26(we26), .out27(we27), .out28(we28), .out29(we29),
    .out30(we30), .out31(we31), .sel(WriteReg), .en(RegWEn));  // open: out0
  Register #(.width(32)) register_1 (.D({32{1'b0}}), .en(1'b0), .clk(clk), .Q(x0));  // open: clr
  Register #(.width(32)) register_2 (.D(RegWriteData), .en(we1), .clk(clk), .Q(ra));  // open: clr
  Register #(.width(32)) register_3 (.D(RegWriteData), .en(we2), .clk(clk), .Q(sp));  // open: clr
  Register #(.width(32)) register_4 (.D(RegWriteData), .en(we3), .clk(clk), .Q(gp));  // open: clr
  Register #(.width(32)) register_5 (.D(RegWriteData), .en(we4), .clk(clk), .Q(tp));  // open: clr
  Register #(.width(32)) register_6 (.D(RegWriteData), .en(we5), .clk(clk), .Q(t0));  // open: clr
  Register #(.width(32)) register_7 (.D(RegWriteData), .en(we6), .clk(clk), .Q(t1));  // open: clr
  Register #(.width(32)) register_8 (.D(RegWriteData), .en(we7), .clk(clk), .Q(t2));  // open: clr
  Register #(.width(32)) register_9 (.D(RegWriteData), .en(we8), .clk(clk), .Q(s0));  // open: clr
  Register #(.width(32)) register_10 (.D(RegWriteData), .en(we9), .clk(clk), .Q(s1));  // open: clr
  Register #(.width(32)) register_11 (.D(RegWriteData), .en(we10), .clk(clk), .Q(a0));  // open: clr
  Register #(.width(32)) register_12 (.D(RegWriteData), .en(we11), .clk(clk), .Q(a1));  // open: clr
  Register #(.width(32)) register_13 (.D(RegWriteData), .en(we12), .clk(clk), .Q(a2));  // open: clr
  Register #(.width(32)) register_14 (.D(RegWriteData), .en(we13), .clk(clk), .Q(a3));  // open: clr
  Register #(.width(32)) register_15 (.D(RegWriteData), .en(we14), .clk(clk), .Q(a4));  // open: clr
  Register #(.width(32)) register_16 (.D(RegWriteData), .en(we15), .clk(clk), .Q(a5));  // open: clr
  Register #(.width(32)) register_17 (.D(RegWriteData), .en(we16), .clk(clk), .Q(a6));  // open: clr
  Register #(.width(32)) register_18 (.D(RegWriteData), .en(we17), .clk(clk), .Q(a7));  // open: clr
  Register #(.width(32)) register_19 (.D(RegWriteData), .en(we18), .clk(clk), .Q(s2));  // open: clr
  Register #(.width(32)) register_20 (.D(RegWriteData), .en(we19), .clk(clk), .Q(s3));  // open: clr
  Register #(.width(32)) register_21 (.D(RegWriteData), .en(we20), .clk(clk), .Q(s4));  // open: clr
  Register #(.width(32)) register_22 (.D(RegWriteData), .en(we21), .clk(clk), .Q(s5));  // open: clr
  Register #(.width(32)) register_23 (.D(RegWriteData), .en(we22), .clk(clk), .Q(s6));  // open: clr
  Register #(.width(32)) register_24 (.D(RegWriteData), .en(we23), .clk(clk), .Q(s7));  // open: clr
  Register #(.width(32)) register_25 (.D(RegWriteData), .en(we24), .clk(clk), .Q(s8));  // open: clr
  Register #(.width(32)) register_26 (.D(RegWriteData), .en(we25), .clk(clk), .Q(s9));  // open: clr
  Register #(.width(32)) register_27 (.D(RegWriteData), .en(we26), .clk(clk), .Q(s10));  // open: clr
  Register #(.width(32)) register_28 (.D(RegWriteData), .en(we27), .clk(clk), .Q(s11));  // open: clr
  Register #(.width(32)) register_29 (.D(RegWriteData), .en(we28), .clk(clk), .Q(t3));  // open: clr
  Register #(.width(32)) register_30 (.D(RegWriteData), .en(we29), .clk(clk), .Q(t4));  // open: clr
  Register #(.width(32)) register_31 (.D(RegWriteData), .en(we30), .clk(clk), .Q(t5));  // open: clr
  Register #(.width(32)) register_32 (.D(RegWriteData), .en(we31), .clk(clk), .Q(t6));  // open: clr
  Multiplexer #(.enable("false"), .select(5), .width(32)) multiplexer_1 (
    .in0(x0), .in1(ra), .in2(sp), .in3(gp), .in4(tp), .in5(t0), .in6(t1), .in7(t2), .in8(s0), .in9(s1),
    .in10(a0), .in11(a1), .in12(a2), .in13(a3), .in14(a4), .in15(a5), .in16(a6), .in17(a7), .in18(s2),
    .in19(s3), .in20(s4), .in21(s5), .in22(s6), .in23(s7), .in24(s8), .in25(s9), .in26(s10), .in27(s11),
    .in28(t3), .in29(t4), .in30(t5), .in31(t6), .out(RegReadData1), .sel(ReadReg1));
  Multiplexer #(.enable("false"), .select(5), .width(32)) multiplexer_2 (
    .in0(x0), .in1(ra), .in2(sp), .in3(gp), .in4(tp), .in5(t0), .in6(t1), .in7(t2), .in8(s0), .in9(s1),
    .in10(a0), .in11(a1), .in12(a2), .in13(a3), .in14(a4), .in15(a5), .in16(a6), .in17(a7), .in18(s2),
    .in19(s3), .in20(s4), .in21(s5), .in22(s6), .in23(s7), .in24(s8), .in25(s9), .in26(s10), .in27(s11),
    .in28(t3), .in29(t4), .in30(t5), .in31(t6), .out(RegReadData2), .sel(ReadReg2));

  // Notes on the sheet:
  //   INPUTS to your circuit
  //   DON'T CHANGE THE LOCATIONS OF THE INPUTS AND OUTPUTS!
  //   These are DEBUG/TEST outputs from your circuit.
  //   OUTPUTS from your circuit
endmodule
